# Fritzing sketch Autoblinds-dia-0.3 (saved by Fritzing 0.7.12b)
breadboards: 1

parts:
  Arduino2 = Arduino
  S1 = Pushbutton [package="[THT]"]
  R1 = Photocell (LDR) [package=THT]
  J1 = Infrared Proximity Sensor
  J2 = Basic Servo
  12v_Relay_Switch = DIP-Relay-D31A [part_number="12v Relay Stich"]
  S2 = Toggle Switch [package=THT]
  R2 = Resistor [tolerance=±5% resistance=10k package=THT]
  R3 = Resistor [tolerance=±5% resistance=4.7k package=THT]
  R4 = Resistor [tolerance=±5% resistance=100 package=THT]

nets:
  N1: Arduino2.D9, J2.pulse
  N2: Arduino2.D4, S2.L1, S2.COM
  N3: Arduino2.D2, S1.Pin_1, S1.Pin_2, 12v_Relay_Switch.B1_Switch_Terminal_B, 12v_Relay_Switch.B2_Switch_Terminal_B
  +5V: Arduino2.+5V, Arduino2.A1, R1.pin_0, J2.vcc, R3.Pin_0, R4.Pin_0
  GND: Arduino2.GND, S1.Pin_3, S1.Pin_4, J1.GND, J2.gnd, 12v_Relay_Switch.Coil2_-, 12v_Relay_Switch.Coil_Sheeld, S2.L2, R2.Pin_1
  N4: Arduino2.A0, R1.pin_1, R2.Pin_0
  N5: J1.Vout, R3.Pin_1
  N6: J1.Vcc, R4.Pin_1
  N7: 12v_Relay_Switch.A1_Switch_Terminal_A, 12v_Relay_Switch.A2_Switch_Terminal_A
  N8: 12v_Relay_Switch.COIL1_+, 12v_Relay_Switch.n.c.
